# Fritzing sketch onepercent (saved by Fritzing 0.9.10b)
breadboards: 1

parts:
  Mod1 = Raspberry Pi Pico
  NeoKey = IC, DIP package, 10 pins [chip_label=Neokey]
  U1 = mystery part, 4 pins [chip_label=OLED]
  TRRS1 = Audio Jack (TRRS) 3.5mm [part_number="LUMBERG JEITA RC-5325A" package="RC-5325A [SMD]"]

nets:
  N1: Mod1.pin_3, Mod1.pin_8, Mod1.pin_13, Mod1.pin_18, Mod1.pin_23, Mod1.pin_28, Mod1.pin_33, Mod1.pin_38, NeoKey.pin5, NeoKey.pin9, U1.pin1, TRRS1.TIP
  N2: Mod1.pin_19, NeoKey.pin3
  N3: Mod1.pin_20, NeoKey.pin4, TRRS1.SLEEVE
  N4: Mod1.pin_21, U1.pin4
  N5: Mod1.pin_22, U1.pin3
  N6: Mod1.pin_36, NeoKey.pin10, U1.pin2

custom parts:
  Raspberry Pi Pico: Raspberry Pi Pico. Based around the RP2040 microcontroller the Pico is a low cost microcontroller device bringing Raspberry Pi quality, cost, and easy of use to the microcontroller space. Jan 2021, Split part in to two versions: tht (this one) and SMD. This one will drill holes for a .1 in header in pcb to allow plugging in the module as well as providing pads to solder the module to the top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
